# Fritzing sketch 555-Circuit (saved by Fritzing 0.9.3b)
breadboards: 1

parts:
  NE555 = 555 Timer [package="DIP8 [THT]"]
  R3 = Resistor [tolerance=±5% resistance=1k package="1206 [SMD]"]
  LED1 = smd LED [color="Red (633nm)" package="0603 [SMD]"]
  R5 = Resistor [tolerance=±5% resistance=47k package="1206 [SMD]"]
  R6 = Resistor [tolerance=±5% resistance=100k package="1206 [SMD]"]
  R1 = Resistor [tolerance=±5% resistance=4.7k package="1206 [SMD]"]
  R4 = Resistor [tolerance=±5% resistance=10k package="1206 [SMD]"]
  BAT1 = BC9VPC [package=bc9vpc]
  C3 = Electrolytic Capacitor [capacitance=220µF package="100 mil [THT, electrolytic]"]  # not connected
  C2 = Electrolytic Capacitor [capacitance=100µF package="100 mil [THT, electrolytic]"]  # not connected
  C1 = Electrolytic Capacitor [capacitance=1µF package="100 mil [THT, electrolytic]"]
  R2 = Resistor [tolerance=±5% resistance=4.7k package="1206 [SMD]"]

nets (from the schematic view):
  N1: NE555.Trigger, NE555.Threshold, C1.+, R2.Pin_1
  N2: NE555.Reset, NE555.Vcc_Supply_Voltage, R5.Pin_0, R6.Pin_0, R1.Pin_0, R4.Pin_0, BAT1.V+
  N3: NE555.Discharge, R1.Pin_1, R2.Pin_0
  N4: R3.Pin_0, LED1.anode
  N5: LED1.cathode, BAT1.V-, C1.-
