# Fritzing sketch Session_1_Circuit (saved by Fritzing 0.9.3b)
breadboards: 1

parts:
  3V_Coin_Cell_&_Holder = Battery Holders [package=battcom_20mm_pth]
  LED1 = LED - 3mm [color="Green (570nm)" package="3 mm [THT]"]
  R1 = Resistor [tolerance=±5% resistance=100 package="0805 [SMD]"]
  Our_Textile_sensor = Photocell (LDR) [package=THT]

nets:
  N1: 3V_Coin_Cell_&_Holder.+, LED1.anode
  N2: 3V_Coin_Cell_&_Holder.-, R1.Pin_0
  N3: R1.Pin_1, Our_Textile_sensor.pin_0
